// Logisim project CPU.circ as structural Verilog: 12 circuits, main circuit main
module main (
  input  [3:0] A,
  input  [3:0] B,
  output [3:0] SAIDA
);

  wire decodificador_1_a_2, decodificador_1_b_2, decodificador_1_c_2, decodificador_1_d_2, decodificador_1_e,
       decodificador_1_f, decodificador_1_g, som_sub1b_1_cout, som_sub1b_2_cout, som_sub1b_3_cout,
       som_sub1b_4_cout;

  Hex_Digit_Display hex_digit_display_1 (.value(A));  // open: dp
  Hex_Digit_Display hex_digit_display_2 (.value(B));  // open: dp
  som_sub1b som_sub1b_1 (.A(B[3]), .B(A[3]), .SUB_CIN(som_sub1b_2_cout), .SUM(SAIDA[3]), .COUT(som_sub1b_1_cout));
  LED LED_OVERFLOW (.in(som_sub1b_1_cout));
  som_sub1b som_sub1b_2 (.A(B[2]), .B(A[2]), .SUB_CIN(som_sub1b_3_cout), .SUM(SAIDA[2]), .COUT(som_sub1b_2_cout));
  som_sub1b som_sub1b_3 (.A(A[1]), .B(B[1]), .SUB_CIN(som_sub1b_4_cout), .SUM(SAIDA[1]), .COUT(som_sub1b_3_cout));
  som_sub1b som_sub1b_4 (.A(B[0]), .B(A[0]), .SUB_CIN(1'b0), .SUM(SAIDA[0]), .COUT(som_sub1b_4_cout));
  Hex_Digit_Display hex_digit_display_3 (.value(SAIDA));  // open: dp
  decodificador decodificador_1 (
    .D(SAIDA[0]), .C(SAIDA[1]), .B(SAIDA[2]), .A(SAIDA[3]), .a_2(decodificador_1_a_2),
    .b_2(decodificador_1_b_2), .c_2(decodificador_1_c_2), .d_2(decodificador_1_d_2), .e(decodificador_1_e),
    .f(decodificador_1_f), .g(decodificador_1_g));
  _7_Segment_Display u_7_segment_display_1 (
    .g(decodificador_1_g), .f(decodificador_1_f), .a(decodificador_1_a_2), .b(decodificador_1_b_2),
    .e(decodificador_1_e), .d(decodificador_1_d_2), .c(decodificador_1_c_2));  // open: dp
endmodule

// SOM/SUB
module som_sub1b (
  input  A,
  input  B,
  input  SUB_CIN,
  output SUM,
  output COUT
);

  wire AND1_out, AND2_out, AND3_out, XOR1_out, xor_1_out;

  xor xor_1 (xor_1_out, B, SUB_CIN);
  and AND1 (AND1_out, A, SUB_CIN);
  and AND2 (AND2_out, xor_1_out, SUB_CIN);
  and AND3 (AND3_out, xor_1_out, A);
  xor XOR1 (XOR1_out, A, xor_1_out);
  xor XOR2 (SUM, XOR1_out, SUB_CIN);
  or OR1 (COUT, AND1_out, AND2_out, AND3_out);

  // Notes on the sheet:
  //   B_in = B XOR SUB
  //   CIN = SUB
  //   SUM =  A XOR B_in XOR SUB/CIN
  //   COUT = (A AND B_in) OR (CIN/SUB AND (A XOR B_in))
endmodule

// DECODIFICADOR
module decodificador (
  input  D,
  input  C,
  input  B,
  input  A,
  output a_2,
  output b_2,
  output c_2,
  output d_2,
  output e,
  output f,
  output g
);

  wire and_1_out, and_2_out, and_3_out, and_4_out, and_5_out, and_6_out, and_7_out, and_8_out, and_9_out,
       and_10_out, and_11_out, and_12_out, and_13_out, and_14_out, and_15_out, and_16_out, not_1_out,
       not_2_out, not_3_out, not_4_out, not_5_out, not_6_out, not_7_out, not_8_out, not_9_out, not_10_out,
       not_11_out, not_12_out, not_13_out, not_14_out, not_15_out, not_16_out, not_17_out, not_18_out,
       not_19_out, not_20_out, not_21_out;

  not not_1 (not_1_out, D);
  and and_1 (and_1_out, not_1_out, not_2_out);
  not not_2 (not_2_out, B);
  and and_2 (and_2_out, D, B);
  not not_3 (not_3_out, D);
  and and_3 (and_3_out, not_3_out, not_4_out);
  not not_4 (not_4_out, C);
  not not_5 (not_5_out, B);
  and and_4 (and_4_out, D, C);
  not not_6 (not_6_out, C);
  or or_1 (c_2, not_6_out, B, D);
  not not_7 (not_7_out, D);
  and and_5 (and_5_out, not_7_out, not_8_out);
  not not_8 (not_8_out, B);
  not not_9 (not_9_out, D);
  and and_6 (and_6_out, not_9_out, C);
  and and_7 (and_7_out, C, not_10_out);
  not not_10 (not_10_out, B);
  not not_11 (not_11_out, C);
  and and_8 (and_8_out, D, not_11_out, B);
  not not_12 (not_12_out, D);
  and and_9 (and_9_out, not_12_out, not_13_out);
  not not_13 (not_13_out, B);
  not not_14 (not_14_out, D);
  and and_10 (and_10_out, not_14_out, C);
  not not_15 (not_15_out, D);
  and and_11 (and_11_out, not_15_out, not_16_out);
  not not_16 (not_16_out, C);
  not not_17 (not_17_out, D);
  and and_12 (and_12_out, not_17_out, B);
  not not_18 (not_18_out, C);
  and and_13 (and_13_out, not_18_out, B);
  not not_19 (not_19_out, C);
  and and_14 (and_14_out, not_19_out, B);
  not not_20 (not_20_out, D);
  and and_15 (and_15_out, not_20_out, C);
  and and_16 (and_16_out, C, not_21_out);
  not not_21 (not_21_out, B);
  or or_2 (a_2, and_1_out, A, C, and_2_out);
  or or_3 (b_2, and_3_out, not_5_out, and_4_out);
  or or_4 (d_2, and_5_out, A, and_6_out, and_7_out, and_8_out);
  or or_5 (e, and_9_out, and_10_out);
  or or_6 (f, and_11_out, A, and_12_out, and_13_out);
  or or_7 (g, A, and_14_out, and_15_out, and_16_out);
endmodule

// ALU1B
module alu1b (
  input  [3:0] in_1,
  input  A,
  input  B,
  input  SUB,
  input  CIN,
  input  LESS,
  output RESULT,
  output COUT,
  output SET
);

  wire AND_out, NOR_out, OR_out, XOR_out;

  xor XOR (XOR_out, B, SUB);
  som1b som1b_1 (.A(A), .B(XOR_out), .CIN(CIN), .SUM(SET), .COUT(COUT));
  and AND (AND_out, A, B);
  or OR (OR_out, A, B);
  nor NOR (NOR_out, A, B);
  Multiplexer #(.select(4), .enable("false")) multiplexer_1 (
    .in0(AND_out), .in1(OR_out), .in2(NOR_out), .in3(SET), .in4(LESS), .in5(1'b0), .out(RESULT), .sel(in_1));  // open: in6, in7, in8, in9, in10, in11, in12, in13, in14, in15
endmodule

module register (
  input  Load,
  input  [7:0] in_2,
  output [7:0] out_3
);

  wire and_1_out, and_2_out, and_3_out, and_4_out, and_5_out, and_6_out, and_7_out, and_8_out, and_9_out,
       and_10_out, and_11_out, and_12_out, and_13_out, and_14_out, and_15_out, and_16_out, CLOCK_out,
       d_ff_1_q, d_ff_2_q, d_ff_3_q, d_ff_4_q, d_ff_5_q, d_ff_6_q, d_ff_7_q, d_ff_8_q, not_1_out, not_2_out,
       not_3_out, not_4_out, not_5_out, not_6_out, not_7_out, not_8_out, or_1_out, or_2_out, or_3_out,
       or_4_out, or_5_out, or_6_out, or_7_out, or_8_out, undriven;

  Clock CLOCK (.out(CLOCK_out));
  not not_1 (not_1_out, Load);
  not not_2 (not_2_out, Load);
  not not_3 (not_3_out, Load);
  not not_4 (not_4_out, Load);
  not not_5 (not_5_out, Load);
  not not_6 (not_6_out, Load);
  not not_7 (not_7_out, Load);
  not not_8 (not_8_out, Load);
  and and_1 (and_1_out, not_2_out, d_ff_2_q);
  and and_2 (and_2_out, Load, in_2[7]);
  and and_3 (and_3_out, not_3_out, d_ff_3_q);
  and and_4 (and_4_out, Load, in_2[7]);
  and and_5 (and_5_out, not_4_out, d_ff_4_q);
  and and_6 (and_6_out, Load, in_2[7]);
  and and_7 (and_7_out, not_5_out, d_ff_5_q);
  and and_8 (and_8_out, Load, in_2[7]);
  and and_9 (and_9_out, not_6_out, d_ff_6_q);
  and and_10 (and_10_out, Load, in_2[7]);
  and and_11 (and_11_out, not_7_out, d_ff_7_q);
  and and_12 (and_12_out, Load, in_2[7]);
  and and_13 (and_13_out, not_8_out, d_ff_8_q);
  and and_14 (and_14_out, Load, in_2[7]);
  and and_15 (and_15_out, not_1_out, d_ff_1_q);
  or or_1 (or_1_out, and_15_out, and_16_out);
  and and_16 (and_16_out, Load, in_2[7]);
  or or_2 (or_2_out, and_1_out, and_2_out);
  or or_3 (or_3_out, and_3_out, and_4_out);
  or or_4 (or_4_out, and_5_out, and_6_out);
  or or_5 (or_5_out, and_7_out, and_8_out);
  or or_6 (or_6_out, and_9_out, and_10_out);
  or or_7 (or_7_out, and_11_out, and_12_out);
  or or_8 (or_8_out, and_13_out, and_14_out);
  D_Flip_Flop d_ff_1 (.clk(CLOCK_out), .D(or_1_out), .Q(d_ff_1_q));  // open: Qn, preset, en, reset
  D_Flip_Flop d_ff_2 (.clk(CLOCK_out), .D(or_2_out), .Q(d_ff_2_q));  // open: Qn, preset, en, reset
  D_Flip_Flop d_ff_3 (.clk(CLOCK_out), .D(or_3_out), .Q(d_ff_3_q));  // open: Qn, preset, en, reset
  D_Flip_Flop d_ff_4 (.clk(CLOCK_out), .D(or_4_out), .Q(d_ff_4_q));  // open: Qn, preset, en, reset
  D_Flip_Flop d_ff_5 (.clk(CLOCK_out), .D(or_5_out), .Q(d_ff_5_q));  // open: Qn, preset, en, reset
  D_Flip_Flop d_ff_6 (.clk(CLOCK_out), .D(or_6_out), .Q(d_ff_6_q));  // open: Qn, preset, en, reset
  D_Flip_Flop d_ff_7 (.clk(CLOCK_out), .D(or_7_out), .Q(d_ff_7_q));  // open: Qn, preset, en, reset
  D_Flip_Flop d_ff_8 (.clk(CLOCK_out), .D(or_8_out), .Q(d_ff_8_q));  // open: Qn, preset, en, reset
  and and_17 (out_3[7], d_ff_1_q, undriven);
  and and_18 (out_3[6], d_ff_2_q, undriven);
  and and_19 (out_3[5], d_ff_3_q, undriven);
  and and_20 (out_3[4], d_ff_4_q, undriven);
  and and_21 (out_3[3], d_ff_5_q, undriven);
  and and_22 (out_3[2], d_ff_6_q, undriven);
  and and_23 (out_3[1], d_ff_7_q, undriven);
  and and_24 (out_3[0], d_ff_8_q, undriven);

  assign in_2[6:0] = {7{in_2[7]}};

  // Notes on the sheet:
  //   8 bit register
endmodule

// SHIFTLEFT
module shiftleft (
  input  [7:0] INPUT,
  output [7:0] out_2
);


  assign out_2 = {INPUT[6:0], 1'b0};
  // also tied to GND on the sheet: INPUT[7]
endmodule

// SHIFTRIGHT
module shiftright (
  input  [7:0] INPUT,
  output [7:0] OUTPUT
);


  assign OUTPUT = {1'b0, INPUT[7:1]};
  // also tied to GND on the sheet: INPUT[0]
endmodule

module register1b (
  input  Load,
  input  D1
);

  wire and_1_out, and_2_out, CLOCK_out, d_ff_1_q, not_1_out, or_1_out;

  Clock CLOCK (.out(CLOCK_out));
  not not_1 (not_1_out, Load);
  and and_1 (and_1_out, not_1_out, d_ff_1_q);
  and and_2 (and_2_out, Load, D1);
  or or_1 (or_1_out, and_1_out, and_2_out);
  D_Flip_Flop d_ff_1 (.clk(CLOCK_out), .D(or_1_out), .Q(d_ff_1_q));  // open: Qn, preset, en, reset

  // Notes on the sheet:
  //   1 bit register
endmodule

// MULT8B
module mult8b (
  input  [3:0] X,
  input  [3:0] Y,
  output [7:0] Produto
);

  wire and_2_out, and_3_out, and_4_out, and_5_out, and_6_out, and_7_out, and_8_out, and_9_out, and_10_out,
       and_11_out, and_12_out, and_13_out, and_14_out, and_15_out, and_16_out, som1b_1_cout, som1b_1_sum,
       som1b_2_cout, som1b_3_cout, som1b_3_sum, som1b_4_cout, som1b_4_sum, som1b_5_cout, som1b_5_sum,
       som1b_6_cout, som1b_7_cout, som1b_7_sum, som1b_8_cout, som1b_8_sum, som1b_10_cout, som1b_11_cout,
       som1b_12_cout;

  and and_1 (Produto[0], X[0], Y[0]);
  and and_2 (and_2_out, X[1], Y[0]);
  and and_3 (and_3_out, X[2], Y[0]);
  and and_4 (and_4_out, X[3], Y[0]);
  and and_5 (and_5_out, X[2], Y[1]);
  and and_6 (and_6_out, X[3], Y[1]);
  and and_7 (and_7_out, X[0], Y[1]);
  and and_8 (and_8_out, X[1], Y[1]);
  som1b som1b_1 (.A(and_4_out), .B(and_5_out), .CIN(som1b_3_cout), .SUM(som1b_1_sum), .COUT(som1b_1_cout));
  and and_9 (and_9_out, X[3], Y[2]);
  som1b som1b_2 (.A(and_2_out), .B(and_7_out), .CIN(1'b0), .SUM(Produto[1]), .COUT(som1b_2_cout));
  som1b som1b_3 (.A(and_3_out), .B(and_8_out), .CIN(som1b_2_cout), .SUM(som1b_3_sum), .COUT(som1b_3_cout));
  som1b som1b_4 (.A(som1b_1_cout), .B(and_6_out), .CIN(1'b0), .SUM(som1b_4_sum), .COUT(som1b_4_cout));
  and and_10 (and_10_out, X[3], Y[3]);
  som1b som1b_5 (.A(som1b_4_cout), .B(and_9_out), .CIN(som1b_8_cout), .SUM(som1b_5_sum), .COUT(som1b_5_cout));
  and and_11 (and_11_out, X[0], Y[2]);
  and and_12 (and_12_out, X[1], Y[2]);
  and and_13 (and_13_out, X[2], Y[2]);
  som1b som1b_6 (.A(som1b_3_sum), .B(and_11_out), .CIN(1'b0), .SUM(Produto[2]), .COUT(som1b_6_cout));
  som1b som1b_7 (.A(som1b_1_sum), .B(and_12_out), .CIN(som1b_6_cout), .SUM(som1b_7_sum), .COUT(som1b_7_cout));
  som1b som1b_8 (.A(som1b_4_sum), .B(and_13_out), .CIN(som1b_7_cout), .SUM(som1b_8_sum), .COUT(som1b_8_cout));
  som1b som1b_9 (.A(som1b_5_cout), .B(and_10_out), .CIN(som1b_12_cout), .SUM(Produto[6]), .COUT(Produto[7]));
  and and_14 (and_14_out, X[0], Y[3]);
  and and_15 (and_15_out, X[1], Y[3]);
  and and_16 (and_16_out, X[2], Y[3]);
  som1b som1b_10 (.A(som1b_7_sum), .B(and_14_out), .CIN(1'b0), .SUM(Produto[3]), .COUT(som1b_10_cout));
  som1b som1b_11 (.A(som1b_8_sum), .B(and_15_out), .CIN(som1b_10_cout), .SUM(Produto[4]), .COUT(som1b_11_cout));
  som1b som1b_12 (.A(som1b_5_sum), .B(and_16_out), .CIN(som1b_11_cout), .SUM(Produto[5]), .COUT(som1b_12_cout));

  // Notes on the sheet:
  //   0
  //   0
  //   o
  //   0
  //   0
  //   0
  //   0
  //   0
  //   0
  //   0
  //   0
  //   0
  //   1
  //   0
  //   1
  //   1
  //   1
  //   1
  //   1
  //   0
  //   1
  //   0
  //   1
endmodule

module alu8b (
  input  [1:0] C2,
  input  [3:0] C1,
  input  SUB,
  input  [7:0] A,
  input  [7:0] B,
  output [7:0] RESULTADO,
  output [3:0] B4,
  output [3:0] A4,
  output COUT
);

  wire alu1b_1_cout, alu1b_2_cout, alu1b_3_cout, alu1b_4_cout, alu1b_5_cout, alu1b_6_cout, alu1b_7_cout,
       alu1b_8_set, and_1_out, or_1_out, xor_1_out;
  wire [6:0] rom_1_data, rom_2_data;
  wire [7:0] alu1b_1_result, mult8b_1_produto, multiplexer_1_out, shiftleft_1_out_2, shiftright_1_output;

  Hex_Digit_Display hex_digit_display_1 (.value(A[3:0]));  // open: dp
  Hex_Digit_Display hex_digit_display_2 (.value(A[7:4]));  // open: dp
  Hex_Digit_Display hex_digit_display_3 (.value(B[7:4]));  // open: dp
  Hex_Digit_Display hex_digit_display_4 (.value(B[3:0]));  // open: dp
  LED led_1 (.in(xor_1_out));
  xor xor_1 (xor_1_out, alu1b_7_cout, COUT);
  mult8b mult8b_1 (.X(A[3:0]), .Y(B[3:0]), .Produto(mult8b_1_produto));
  alu1b alu1b_1 (
    .in_1(C1), .A(A[0]), .B(B[0]), .CIN(SUB), .LESS(alu1b_8_set), .RESULT(alu1b_1_result[0]),
    .COUT(alu1b_1_cout), .SUB(SUB));  // open: SET
  alu1b alu1b_2 (
    .in_1(C1), .A(A[1]), .B(B[1]), .CIN(alu1b_1_cout), .LESS(1'b0), .RESULT(alu1b_1_result[1]),
    .COUT(alu1b_2_cout), .SUB(SUB));  // open: SET
  alu1b alu1b_3 (
    .in_1(C1), .A(A[2]), .B(B[2]), .CIN(alu1b_2_cout), .LESS(1'b0), .RESULT(alu1b_1_result[2]),
    .COUT(alu1b_3_cout), .SUB(SUB));  // open: SET
  alu1b alu1b_4 (
    .in_1(C1), .A(A[3]), .B(B[3]), .CIN(alu1b_3_cout), .LESS(1'b0), .RESULT(alu1b_1_result[3]),
    .COUT(alu1b_4_cout), .SUB(SUB));  // open: SET
  alu1b alu1b_5 (
    .in_1(C1), .A(A[4]), .B(B[4]), .CIN(alu1b_4_cout), .LESS(1'b0), .RESULT(alu1b_1_result[4]),
    .COUT(alu1b_5_cout), .SUB(SUB));  // open: SET
  alu1b alu1b_6 (
    .in_1(C1), .A(A[5]), .B(B[5]), .CIN(alu1b_5_cout), .LESS(1'b0), .RESULT(alu1b_1_result[5]),
    .COUT(alu1b_6_cout), .SUB(SUB));  // open: SET
  alu1b alu1b_7 (
    .in_1(C1), .A(A[6]), .B(B[6]), .CIN(alu1b_6_cout), .LESS(1'b0), .RESULT(alu1b_1_result[6]),
    .COUT(alu1b_7_cout), .SUB(SUB));  // open: SET
  alu1b alu1b_8 (
    .in_1(C1), .A(A[7]), .B(B[7]), .CIN(alu1b_7_cout), .LESS(1'b0), .RESULT(alu1b_1_result[7]), .COUT(COUT),
    .SET(alu1b_8_set), .SUB(SUB));
  Multiplexer #(.width(8)) multiplexer_1 (
    .in0(alu1b_1_result), .in1(mult8b_1_produto), .out(multiplexer_1_out), .sel(and_1_out));  // open: en
  or or_1 (or_1_out, C1[0], C1[1]);
  and and_1 (and_1_out, or_1_out, C1[2]);
  shiftleft shiftleft_1 (.INPUT(multiplexer_1_out), .out_2(shiftleft_1_out_2));
  shiftright shiftright_1 (.INPUT(multiplexer_1_out), .OUTPUT(shiftright_1_output));
  Hex_Digit_Display hex_digit_display_5 (.value(RESULTADO[7:4]));  // open: dp
  Multiplexer #(.select(2), .width(8)) multiplexer_2 (
    .in0(multiplexer_1_out), .in1(shiftleft_1_out_2), .in2(shiftright_1_output), .out(RESULTADO), .sel(C2));  // open: in3, en
  Hex_Digit_Display hex_digit_display_6 (.value(RESULTADO[3:0]));  // open: dp
  ROM #(.addrWidth(4), .dataWidth(7)) rom_1 (.addr(RESULTADO[3:0]), .data(rom_1_data));  // open: sel
  ROM #(.addrWidth(4), .dataWidth(7)) rom_2 (.addr(RESULTADO[7:4]), .data(rom_2_data));  // open: sel
  _7_Segment_Display u_7_segment_display_1 (
    .g(rom_1_data[0]), .f(rom_1_data[1]), .a(rom_1_data[6]), .b(rom_1_data[5]), .e(rom_1_data[2]),
    .d(rom_1_data[3]), .c(rom_1_data[4]));  // open: dp
  _7_Segment_Display u_7_segment_display_2 (
    .g(rom_2_data[0]), .f(rom_2_data[1]), .a(rom_2_data[6]), .b(rom_2_data[5]), .e(rom_2_data[2]),
    .d(rom_2_data[3]), .c(rom_2_data[4]));  // open: dp

  assign A4 = A[3:0];
  assign B4 = B[3:0];

  // Notes on the sheet:
  //   OVERFLOW
  //   0000 - AND
  //   0001 - OR
  //   0010 - NOR
  //   0011 - SUM/SUB
  //   0100 - SLT
  //   0101 - MULT
  //   00 - Resultado Normal
  //   01 - Shift Left
  //   10 - Shift Right
  //   contents of rom_1 (hex, n*v repeats v):
  //   7e 30 6d 79 33 5b 5f 70 7f 7b 77 1f 4e 3d 4f 47
  //   contents of rom_2 (hex, n*v repeats v):
  //   7e 30 6d 79 33 5b 5f 70 7f 7b 77 1f 4e 3d 4f 47
endmodule

// SOMADOR
module som1b (
  input  A,
  input  B,
  input  CIN,
  output SUM,
  output COUT
);

  wire AND1_out, AND2_out, AND3_out, XOR1_out;

  and AND1 (AND1_out, A, CIN);
  and AND2 (AND2_out, B, CIN);
  and AND3 (AND3_out, B, A);
  xor XOR1 (XOR1_out, A, B);
  xor XOR2 (SUM, XOR1_out, CIN);
  or OR1 (COUT, AND1_out, AND2_out, AND3_out);
endmodule

module cpu (
  input  [1:0] in_1,
  input  RESET,
  input  in_3,
  input  RESET_2,
  output [7:0] out_5,
  output [7:0] out_6
);

  wire clock_1_out;
  wire [3:0] PC_q;
  wire [6:0] rom_2_data, rom_3_data;
  wire [11:0] rom_1_data;

  Counter #(.width(4), .max('hf)) PC (
    .D(4'b0001), .Q(PC_q), .clk(clock_1_out), .clr(RESET_2));  // open: load, count, carry
  ROM #(.addrWidth(4), .dataWidth(12)) rom_1 (.addr(PC_q), .data(rom_1_data));  // open: sel
  alu8b alu8b_1 (
    .C2(in_1), .C1(rom_1_data[11:8]), .A(out_6), .B(rom_1_data[7:0]), .RESULTADO(out_5), .SUB(in_3));  // open: B4, A4, COUT
  Clock clock_1 (.out(clock_1_out));
  Register register_1 (.D(out_5), .en(1'b1), .Q(out_6), .clk(clock_1_out), .clr(RESET));
  Hex_Digit_Display hex_digit_display_1 (.value(out_6[7:4]));  // open: dp
  Hex_Digit_Display hex_digit_display_2 (.value(out_6[3:0]));  // open: dp
  ROM #(.addrWidth(4), .dataWidth(7)) rom_2 (.addr(out_6[7:4]), .data(rom_2_data));  // open: sel
  ROM #(.addrWidth(4), .dataWidth(7)) rom_3 (.addr(out_6[3:0]), .data(rom_3_data));  // open: sel
  _7_Segment_Display u_7_segment_display_1 (
    .g(rom_2_data[0]), .f(rom_2_data[1]), .a(rom_2_data[6]), .b(rom_2_data[5]), .e(rom_2_data[2]),
    .d(rom_2_data[3]), .c(rom_2_data[4]));  // open: dp
  _7_Segment_Display u_7_segment_display_2 (
    .g(rom_3_data[0]), .f(rom_3_data[1]), .a(rom_3_data[6]), .b(rom_3_data[5]), .e(rom_3_data[2]),
    .d(rom_3_data[3]), .c(rom_3_data[4]));  // open: dp

  // Notes on the sheet:
  //   PC
  //   30a (opcore: 3; operando: 0a)- load (soma 10)
  //   332 (opcore: 3; operando: 32)- sum (soma 50)
  //   3ff (opcore: 3; operando: ff)- sub (sub -1)
  //   03c (opcore: 0; operando: 3c)- and (and 60)
  //   1f0 (opcore: 1; operando: f0)- or (or 240)
  //   2ff (opcore: 2; operando: ff)- nor (nor 255)
  //   504 (opcore: 5; operando: 04)- mult (mult 4)
  //   4ff (opcore: 4; operando: ff)- slt (slt 255)
  //   ROM
  //   contents of rom_1 (hex, n*v repeats v):
  //   30a 332 3ff 3c 1f0 2ff 504 4ff
  //   ALU
  //   REGISTROR
  //   contents of rom_2 (hex, n*v repeats v):
  //   7e 30 6d 79 33 5b 5f 70 7f 7b 77 1f 4e 3d 4f 47
  //   contents of rom_3 (hex, n*v repeats v):
  //   7e 30 6d 79 33 5b 5f 70 7f 7b 77 1f 4e 3d 4f 47
endmodule
